# Fritzing sketch schema (saved by Fritzing 0.9.3b)
breadboards: 1

parts:
  Součástka1 = Arduino Uno (Rev3)
  S1 = Pushbutton [package="[THT]"]
  J1 = Piezo Speaker
  R1 = Rotary Potentiometer (Small) [maximum_resistance=100kΩ package=THT]
  R2 = Rotary Potentiometer (Small) [maximum_resistance=100kΩ package=THT]
  S2 = Pushbutton [package="[THT]"]
  S3 = Pushbutton [package="[THT]"]
  S4 = Pushbutton [package="[THT]"]
  R3 = Resistor [tolerance=±5% resistance=220 package=THT]
  R4 = Resistor [tolerance=±5% resistance=10k package=THT]
  R5 = Resistor [tolerance=±5% resistance=1M package=THT]
  R6 = Resistor [tolerance=±5% resistance=10k package=THT]

nets:
  N1: Součástka1.A0, S1.Pin_1, S1.Pin_2, S2.Pin_1, S2.Pin_2, S3.Pin_1, S3.Pin_2, S4.Pin_1, S4.Pin_2, R6.Pin_1
  N2: Součástka1.A1, R2.wiper
  N3: Součástka1.D8, R1.leg1
  N4: Součástka1.5V, S1.Pin_3, S1.Pin_4, J1.pin2, R2.leg1, R3.Pin_0, R4.Pin_0, R5.Pin_0
  N5: Součástka1.GND, R1.leg2, R2.leg2, R6.Pin_0
  N6: J1.pin1, R1.wiper
  N7: S2.Pin_3, S2.Pin_4, R3.Pin_1
  N8: S3.Pin_3, S3.Pin_4, R4.Pin_1
  N9: S4.Pin_3, S4.Pin_4, R5.Pin_1
