# Fritzing sketch schema (saved by Fritzing 0.9.3b)
breadboards: 1

parts:
  Součástka1 = Arduino Uno (Rev3)
  R1 = Photocell (LDR) [package=THT]
  R2 = Photocell (LDR) [package=THT]
  R3 = Photocell (LDR) [package=THT]
  S1 = Pushbutton [package="[THT]"]
  S2 = Pushbutton [package="[THT]"]
  S3 = Pushbutton [package="[THT]"]
  R4 = Resistor [tolerance=±5% resistance=10k package=THT]
  R5 = Resistor [tolerance=±5% resistance=10k package=THT]
  R6 = Resistor [tolerance=±5% resistance=10k package=THT]
  R7 = Resistor [tolerance=±5% resistance=10k package=THT]
  R8 = Resistor [tolerance=±5% resistance=10k package=THT]
  R9 = Resistor [tolerance=±5% resistance=10k package=THT]

nets:
  N1: Součástka1.A0, R2.pin_0, R5.Pin_1
  N2: Součástka1.A1, R3.pin_0, R4.Pin_1
  N3: Součástka1.A2, R1.pin_0, R9.Pin_1
  N4: Součástka1.D2, S1.Pin_3, S1.Pin_4, R6.Pin_1
  N5: Součástka1.D3_PWM, S2.Pin_3, S2.Pin_4, R7.Pin_1
  N6: Součástka1.D4, S3.Pin_3, S3.Pin_4, R8.Pin_1
  N7: Součástka1.5V, R1.pin_1, R2.pin_1, R3.pin_1, S1.Pin_1, S1.Pin_2, S2.Pin_1, S3.Pin_1
  N8: Součástka1.GND, R4.Pin_0, R5.Pin_0, R6.Pin_0, R7.Pin_0, R8.Pin_0, R9.Pin_0
